# Fritzing sketch H bridge sketch (saved by Fritzing 0.9.1b)
circuit board: 8.46667cm x 5.64444cm
breadboards: 1

parts:
  Onderdeel1 = Arduino Mega 2560 (Rev3)
  IC1 = H-Bridge [package=THT]
  M1 = DC Motor
  M2 = DC Motor
  U1 = Battery Holders [package=battery-aa]
  U2 = Battery Holders [package=battery-aa]
  U3 = Battery Holders [package=battery-aa]
  U4 = Battery Holders [package=battery-aa]

nets:
  N1: Onderdeel1.5V, IC1.VCC1
  GND: Onderdeel1.GND, IC1.GND1, IC1.GND2, IC1.GND3, IC1.GND4, U1.+
  N2: Onderdeel1.VIN, IC1.VCC2, U4.-
  N3: Onderdeel1.D2_PWM, IC1.3_4EN
  N4: Onderdeel1.D3_PWM, IC1.1_2EN
  N5: Onderdeel1.D22, IC1.1A
  N6: Onderdeel1.D23, IC1.2A
  N7: Onderdeel1.D24, IC1.4A
  N8: Onderdeel1.D25, IC1.3A
  N9: IC1.1Y, M1.pin_1
  N10: IC1.2Y, M1.pin_2
  N11: IC1.3Y, M2.pin_2
  N12: IC1.4Y, M2.pin_1
  N13: U1.-, U2.+
  N14: U2.-, U3.+
  N15: U3.-, U4.+
